# Fritzing sketch Schematic (saved by Fritzing 0.9.2b)
breadboards: 2

parts:
  Mod1 = Raspberry Pi Pico
  Part1 = SRF05 Ultrasonic Rangefinder
  Squix1 = OLED 0.96" 128x64 I2C SSD1306

nets:
  N1: Mod1.pin_1, Squix1.SCA
  N2: Mod1.pin_2, Squix1.SCL
  GND: Mod1.pin_3, Mod1.pin_8, Mod1.pin_13, Mod1.pin_18, Mod1.pin_23, Mod1.pin_28, Mod1.pin_33, Mod1.pin_38, Part1.GND, Squix1.GND
  N3: Mod1.pin_4, Part1.Echo
  N4: Mod1.pin_5, Part1.Trig
  VCC: Mod1.pin_39, Part1.VCC, Squix1.VCC

custom parts:
  Raspberry Pi Pico: Raspberry Pi Pico. Based around the RP2040 microcontroller the Pico is a low cost microcontroller device bringing Raspberry Pi quality, cost, and easy of use to the microcontroller space. Jan 2021, Split part in to two versions: SMD (this one) and tht. This one is single sided and uses the castellation pads to solder the module to the board (no holes, other than for the USB connector!). The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
